// Logisim project Branch_Control(Finished).circ as structural Verilog: 1 circuit, main circuit Branch_Control
module Branch_Control (
  input  [31:0] JS_Jump_Size,
  input  [31:0] IA_InstructionAddress,
  input  jmp,
  input  FC,
  output [31:0] NIR_NextInstructionAddrs
);

  wire and_1_out;
  wire [31:0] adder_1_out, multiplier_1_out;

  Multiplier #(.width(32)) multiplier_1 (
    .a(JS_Jump_Size), .b(32'h4), .out(multiplier_1_out), .cin({32{1'b0}}));  // open: cout
  Adder #(.width(32)) adder_1 (
    .a(multiplier_1_out), .b(IA_InstructionAddress), .out(adder_1_out), .cin(1'b0));  // open: cout
  Multiplexer #(.width(32), .enable("false")) multiplexer_1 (
    .in0(IA_InstructionAddress), .in1(adder_1_out), .out(NIR_NextInstructionAddrs), .sel(and_1_out));
  and and_1 (and_1_out, jmp, FC);

  // Notes on the sheet:
  //   JS x 4
  //   IA + (JS x 4)
endmodule
