// Logisim project CPU(S-MIPS).circ as structural Verilog: 1 circuit, main circuit S-MIPS
module S_MIPS (
  input  [31:0] RAM_Out_0,
  input  [31:0] RAM_Out_1,
  input  [31:0] RAM_Out_2,
  input  [31:0] RAM_Out_3,
  input  [3:0] Read_Time,
  input  [3:0] Write_Time,
  input  Start,
  input  Clock,
  input  Kbd_Available,
  input  [6:0] Kbd_ASCII_Data,
  output [31:0] RAM_In_0,
  output [31:0] RAM_In_1,
  output [31:0] RAM_In_2,
  output [31:0] RAM_In_3,
  output Halt,
  output [15:0] Address,
  output Kbd_Enable,
  output Kbd_Clear,
  output TTY_Enable,
  output [6:0] TTY_ASCII_Data,
  output [3:0] Mask,
  output nRead_Write,
  output Chip_Select
);

  wire Fetch, Ram_Ready, ReadIns, rnd_kbd, RST;
  wire [2:0] S_FC;
  wire [3:0] ALU_OP;
  wire [5:0] FuncCode, OpCode;
  wire [17:0] SelectorCodes;
  wire [31:0] inst, MemoryAddress, MemoryData, Out_Word;

  Control_Unit control_unit_1 (
    .START(Start), .fetch(Fetch), .FuncCode(FuncCode), .OpCode(OpCode), .FC_Selector(S_FC), .ALU_Op(ALU_OP),
    .SelectorCodes(SelectorCodes), .rnd_kbd_Selector(rnd_kbd), .TTY_Enable(TTY_Enable),
    .ReadInstruction(ReadIns), .ChipSelect(Chip_Select), .R_W(nRead_Write), .RamReady(Ram_Ready),
    .halt(Halt), .Clock(Clock), .kbd_Enable(Kbd_Enable), .RESET(RST));
  Memory_Controller memory_controller_1 (
    .Input_Word(MemoryData), .O0(RAM_Out_0), .O1(RAM_Out_1), .O2(RAM_Out_2), .O3(RAM_Out_3),
    .R_W(nRead_Write), .Chip_Select(Chip_Select), .Read_Time(Read_Time), .Write_Time(Write_Time),
    .Address(Address), .OW_Out_Word(Out_Word), .Mask(Mask), .I0(RAM_In_0), .I1(RAM_In_1), .I2(RAM_In_2),
    .I3(RAM_In_3), .Ram_Ready(Ram_Ready), .MemoryAddress(MemoryAddress), .reset(RST), .clk(Clock));
  DataPath datapath_1 (
    .reset(RST), .KBD_Data(Kbd_ASCII_Data), .KBD_Enable(Kbd_Available), .Memory_Address(MemoryAddress),
    .Instruction(inst), .Selectors_Code(SelectorCodes), .TTY_Data(TTY_ASCII_Data), .MemoryData(Out_Word),
    .Memory_Data_Out(MemoryData), .Op(ALU_OP), .S_FlagCondition(S_FC), .FuncCode(FuncCode), .OpCode(OpCode),
    .kbd_rnd_Selector(rnd_kbd), .fetch(Fetch), .ReadIns(ReadIns), .clock(Clock), .KBD_Clear(Kbd_Clear));

  // Other names for the same wires on the sheet: CLK = Clock; CS = Chip_Select; KBD_AVAIL = Kbd_Available;
  //   KBD_CLR = Kbd_Clear; KBD_DATA[6:0] = Kbd_ASCII_Data; RAM_A[15:0] = Address; RAM_MASK[3:0] = Mask;
  //   RI0[31:0] = RAM_In_0; RI1[31:0] = RAM_In_1; RI2[31:0] = RAM_In_2; RI_3[31:0] = RAM_In_3; RO0[31:0] = RAM_Out_0;
  //   RO1[31:0] = RAM_Out_1; RO2[31:0] = RAM_Out_2; RO3[31:0] = RAM_Out_3; RW = nRead_Write;
  //   TTY_DATA[6:0] = TTY_ASCII_Data

  // Notes on the sheet:
  //   RAM TIMING
  //   KEYBOARD
  //   DATA FROM RAM
  //   DATA TO RAM
  //   RAM ADDRESS
  //   KEYBOARD
  //   TTY
  //   DATA WRITE MASK
  //   RAM CONTROL
endmodule
