// Logisim project Control_Unit.circ as structural Verilog: 1 circuit, main circuit Control Unit
module Control_Unit (
  input  [5:0] FuncCode,
  input  [5:0] OpCode,
  input  START,
  input  Clock,
  input  RamReady,
  output [17:0] SelectorCodes,
  output [2:0] FC_Selector,
  output [3:0] ALU_Op,
  output fetch,
  output rnd_kbd_Selector,
  output TTY_Enable,
  output ReadInstruction,
  output ChipSelect,
  output R_W,
  output halt,
  output kbd_Enable,
  output CRONORST,
  output RESET
);

  wire CS0, CS1, CS2, CS3, CS4, demultiplexer_1_out0, demultiplexer_1_out1, demultiplexer_2_out0,
       demultiplexer_3_out0, demultiplexer_4_out0, demultiplexer_5_out0, demultiplexer_6_out0, FETCH_2_q,
       IDLE_q, Load, Main, or_1_out, or_7_out, or_8_out, or_10_out, or_11_out, or_12_out, Pop, Push, R1, R2,
       R2_1, R3, R4, ReadMemory_2_q, ReadMemory_q, Store, WriteMemory_2_q;
  wire [1:0] SS_Code;
  wire [5:0] Func_Code, Op_Code;
  wire [17:0] F_S_Codes, Selector_Codes;

  or or_1 (or_1_out, demultiplexer_1_out1, halt);
  or or_2 (R_W, Push, Store);
  D_Flip_Flop IDLE (.clk(Clock), .D(or_1_out), .Q(IDLE_q), .preset(START));  // open: Qn, en, reset
  Demultiplexer #(.enable("false")) demultiplexer_1 (
    .out0(demultiplexer_1_out0), .out1(demultiplexer_1_out1), .in(IDLE_q), .sel(START));
  Priority_Encoder #(.select(2)) priority_encoder_1 (
    .in0(R1), .in1(R2), .in2(R3), .in3(Main), .out(SS_Code));  // open: gs, en_out, en_in
  or or_3 (CS1, demultiplexer_2_out0, Pop);
  or or_4 (CS2, demultiplexer_3_out0, Push);
  or or_5 (CS3, demultiplexer_4_out0, Load);
  or or_6 (CS4, demultiplexer_5_out0, Store);
  or or_7 (or_7_out, demultiplexer_6_out0, CRONORST, demultiplexer_1_out0);
  D_Flip_Flop ReadMemory (.clk(Clock), .D(CS1), .Q(ReadMemory_q));  // open: Qn, preset, en, reset
  D_Flip_Flop WriteMemory (.clk(Clock), .D(CS2), .Q(R2));  // open: Qn, preset, en, reset
  D_Flip_Flop ReadMemory_2 (.clk(Clock), .D(CS3), .Q(ReadMemory_2_q));  // open: Qn, preset, en, reset
  D_Flip_Flop WriteMemory_2 (.clk(Clock), .D(CS4), .Q(WriteMemory_2_q));  // open: Qn, preset, en, reset
  D_Flip_Flop u_FETCH (.clk(Clock), .D(or_7_out), .Q(CS0), .reset(START));  // open: Qn, preset, en
  Demultiplexer #(.enable("false")) demultiplexer_2 (
    .out0(demultiplexer_2_out0), .out1(R1), .in(ReadMemory_q), .sel(RamReady));
  Demultiplexer #(.enable("false")) demultiplexer_3 (.out0(demultiplexer_3_out0), .out1(R2_1), .in(R2), .sel(RamReady));
  Demultiplexer #(.enable("false")) demultiplexer_4 (
    .out0(demultiplexer_4_out0), .out1(R3), .in(ReadMemory_2_q), .sel(RamReady));
  Demultiplexer #(.enable("false")) demultiplexer_5 (
    .out0(demultiplexer_5_out0), .out1(R4), .in(WriteMemory_2_q), .sel(RamReady));
  Demultiplexer #(.enable("false")) demultiplexer_6 (
    .out0(demultiplexer_6_out0), .out1(ReadInstruction), .in(CS0), .sel(RamReady));
  Multiplexer #(.select(2), .width(18), .enable("false")) multiplexer_1 (
    .in0(Selector_Codes), .in1(18'h20024), .in2(18'h10), .in3(18'h20021), .out(F_S_Codes), .sel(SS_Code));
  D_Flip_Flop FETCH_2 (.clk(Clock), .D(ReadInstruction), .Q(FETCH_2_q), .reset(START));  // open: Qn, preset, en
  or or_8 (or_8_out, CRONORST, CS0);
  or or_9 (ChipSelect, CS4, CS3, CS2, CS1, CS0);
  Multiplexer #(.width(18), .enable("false")) multiplexer_2 (
    .in0(Selector_Codes), .in1({18{1'b0}}), .out(SelectorCodes), .sel(or_8_out));
  // Switcher_CU switcher_cu_1: pin names not known; wires that end beside it: Func_Code, FETCH_2_q, Op_Code, kbd_Enable, FC_Selector, ALU_Op, Selector_Codes, Pop, Push, Main, Load, Store, TTY_Enable, rnd_kbd_Selector, halt
  Multiplexer #(.width(6), .enable("false")) multiplexer_3 (
    .in0(FuncCode), .in1({6{1'b0}}), .out(Func_Code), .sel(or_10_out));
  or or_10 (or_10_out, CRONORST, CS0);
  or or_11 (or_11_out, Main, R4, R3, R2_1, R1);
  D_Flip_Flop FETCH_3 (.clk(Clock), .D(or_11_out), .Q(CRONORST), .reset(START));  // open: Qn, preset, en
  Multiplexer #(.width(6), .enable("false")) multiplexer_4 (
    .in0(OpCode), .in1({6{1'b0}}), .out(Op_Code), .sel(or_12_out));
  or or_12 (or_12_out, CRONORST, CS0);

  assign fetch = CRONORST;
  assign RESET = START;

  // Other names for the same wires on the sheet: Chip_Select = ChipSelect; clk = Clock; Instruction = CRONORST;
  //   ReadIns = ReadInstruction; Selector__Codes[17:0] = SelectorCodes

  // Notes on the sheet:
  //   Input_Output_Region
  //   Instruction-Lines
endmodule
