// Logisim project DataPath.circ as structural Verilog: 1 circuit, main circuit DataPath
module DataPath (
  input  [12:0] Selectors_Code,
  input  [31:0] Instruction,
  input  [31:0] MemoryData,
  input  [6:0] KBD_Data,
  input  KBD_Enable,
  input  fetch,
  input  reset,
  input  S_SI,
  output [31:0] Memory_Address,
  output [31:0] Memory_Data_Out,
  output [6:0] TTY_Data
);

  wire A____B, A____B_t, A___B_signed, A___B_signed_t, A___B_unsigned, B_Cero, clk, EI, FC, mf_Hi_Lo,
       not_1_out, R_Hi_Lo, S_MD_SI, S_MemDataOut, S_SA;
  wire [1:0] Esp_Ins_S, S_Memory_Address;
  wire [2:0] S_FlagCondition;
  wire [3:0] Op;
  wire [4:0] DA, Rd, RS, Rt, SA, SB, undriven;
  wire [15:0] Const;
  wire [25:0] dest;
  wire [27:0] PC;
  wire [31:0] ALU_Out, B, B_prime, bit_extender_2_out, Const_extended, DATA_HI, DATA_HI_LO, DATA_INPUT,
       DATA_LO, Hi, jmp_address, Lo, multiplexer_4_out, multiplexer_9_out, NI, random_1_out, Special_Ins_Data;
  wire [31:7] A;
  wire [31:28] final_dest;

  Multiplexer #(.select(2), .width(5), .enable("false")) multiplexer_1 (
    .in0(Rt), .in1({5{1'b0}}), .in2({5{1'b1}}), .out(SB), .sel(Selectors_Code[4:3]));  // open: in3
  Multiplexer #(.select(2), .width(5), .enable("false")) multiplexer_2 (
    .in0(Rd), .in1(Rt), .in2({5{1'b0}}), .in3(undriven), .out(DA), .sel(Selectors_Code[1:0]));
  Multiplexer #(.width(5), .enable("false")) multiplexer_3 (.in0(RS), .in1({5{1'b1}}), .out(SA), .sel(S_SA));
  Multiplexer #(.width(32), .enable("false")) multiplexer_4 (
    .in0(MemoryData), .in1(Special_Ins_Data), .out(multiplexer_4_out), .sel(S_MD_SI));
  Branch_Control branch_control_1 (
    .JS_Jump_Size(Const_extended), .IA_InstructionAddress({final_dest, PC}), .jmp(Selectors_Code[10]),
    .FC(FC), .NIR_NextInstructionAddrs(NI));
  Multiplexer #(.select(2), .width(32), .enable("false")) multiplexer_5 (
    .in0(ALU_Out), .in1(multiplexer_4_out), .in2(Lo), .in3(Hi), .out(DATA_INPUT), .sel(Selectors_Code[6:5]));
  ProgramCounter programcounter_1 (
    .jmp_addr(jmp_address), .jmp_Jump(Selectors_Code[10]), .rst_Reset(reset), .Q({final_dest, PC}),
    .fetch(fetch));
  assign Const_extended = {{16{1'b0}}, Const};  // Bit_Extender bit_extender_1
  InstructionDecoder instructiondecoder_1 (
    .Instruction(Instruction), .DA_DataAddress(DA), .R_W_ReadWrite(Selectors_Code[2]), .SA_SelectorA(RS),
    .SB_SelectorB(Rt), .Jmp(Selectors_Code[10]), .FC_FlagCondition(FC), .dest(dest), .A(Const), .Op(Op),
    .Active_EI(EI), .EspecialInstruction(Esp_Ins_S), .Read_Hi_Lo(R_Hi_Lo), .mf_Hi_Lo(mf_Hi_Lo));  // open: Load, Store
  Multiplexer #(.select(2), .width(32), .enable("false")) multiplexer_6 (
    .in0(B), .in1(Const_extended), .in2({32{1'b0}}), .in3(32'h4), .out(B_prime), .sel(Selectors_Code[8:7]));
  not not_1 (not_1_out, A____B_t);
  RegisterFile registerfile_1 (
    .DA_DestinationAddress(DA), .DI_DataInput(DATA_INPUT), .RW_Read_Write(Selectors_Code[2]),
    .Rst_Reset(reset), .SA(SA), .SB(SB), .Out_A({A, TTY_Data}), .Out_B(B));
  Multiplexer #(.select(3), .enable("false")) multiplexer_7 (
    .in0(1'b0), .in1(A___B_signed), .in2(A___B_unsigned), .in3(A____B), .in4(A___B_signed_t), .in5(A____B_t),
    .in6(not_1_out), .out(FC), .sel(S_FlagCondition));  // open: in7
  Multiplexer #(.select(2), .width(32), .enable("false")) multiplexer_8 (
    .in0(NI), .in1({A, TTY_Data}), .in2({final_dest, dest, 2'b00}), .out(jmp_address),
    .sel(Selectors_Code[12:11]));  // open: in3
  ALU alu_1 (
    .A({A, TTY_Data}), .B(B_prime), .Op(Op), .HI_CONTENT(DATA_HI), .Output(ALU_Out), .LO_CONTENT(DATA_LO),
    .B_ZERO(B_Cero));  // open: UPDATE_HI_LO, A___B_unsigned, A___B_signed, A____B, A____B_2, A___B_s
  assign bit_extender_2_out = {{25{1'b0}}, KBD_Data};  // Bit_Extender bit_extender_2
  Random #(.width(32)) random_1 (.clk(clk), .next(1'b1), .out(random_1_out), .clr(reset));
  Multiplexer #(.width(32), .enable("false")) multiplexer_9 (
    .in0({32{1'b1}}), .in1(bit_extender_2_out), .out(multiplexer_9_out), .sel(KBD_Enable));
  Hi_Lo_registers_Finished__main main_1 (
    .HI_Content(DATA_HI), .Lo_Content(DATA_LO), .Update(Selectors_Code[9]), .Reset(reset),
    .Read_HI_Lo(R_Hi_Lo), .HI_Lo_Data(DATA_HI_LO));
  Multiplexer #(.width(32), .enable("false")) multiplexer_10 (
    .in0(multiplexer_9_out), .in1(random_1_out), .out(Special_Ins_Data), .sel(S_SI));
  Clock clock_1 (.out(clk));
  Multiplexer #(.select(2), .width(32), .enable("false")) multiplexer_11 (
    .in0({final_dest, PC}), .in1({A, TTY_Data}), .in2(B), .in3(ALU_Out), .out(Memory_Address),
    .sel(S_Memory_Address));
  Multiplexer #(.width(32), .enable("false")) multiplexer_12 (
    .in0({A, TTY_Data}), .in1(B), .out(Memory_Data_Out), .sel(S_MemDataOut));

  // Other names for the same wires on the sheet: A[6:0] = TTY_Data; final_dest[27:2] = dest; PC[31:28] = final_dest;
  //   Ins[31:0] = Instruction; KBD_Available = KBD_Enable; MemoryData_MD[31:0] = MemoryData; rst = reset;
  //   S_Special_Instruction = S_SI; S_DA[1:0] = Selectors_Code[1:0]; R_W = Selectors_Code[2];
  //   S_SB[1:0] = Selectors_Code[4:3]; S_DATA_IN[1:0] = Selectors_Code[6:5]; S_ALUB[1:0] = Selectors_Code[8:7];
  //   UpdateHi_Lo = Selectors_Code[9]; Jmp = Selectors_Code[10]; S_jmp_address[1:0] = Selectors_Code[12:11]

  // Notes on the sheet:
  //   Stack-Pointer
  //   Register File
  //   Stack-Pointer
  //   Aqui hay que poner un selector pa qe pase Special InstData pq ahora nadie esta mandando el S_MD/SI
  //   ALU
  //   DATA PATH
  //   MUX ENTRADAS
  //   Branch Contol
  //   Program Counter
  //   Special Instruction Data Input
  //   Stack-Pointer
  //   Stack-Pointer -4
  //   [RS]
  //   [Rt]
  //   Inputs
  //   Outputs
endmodule
