// Logisim project Hi_Lo_registers(Finished).circ as structural Verilog: 1 circuit, main circuit main
module main (
  input  [31:0] HI_Content,
  input  [31:0] Lo_Content,
  input  Update,
  input  Reset,
  input  clock,
  output [31:0] HI_Data,
  output [31:0] Lo_Data
);

  Register #(.width(32), .trigger("falling")) Hi_Register (
    .D(HI_Content), .en(Update), .Q(HI_Data), .clk(clock), .clr(Reset));
  Register #(.width(32), .trigger("falling")) Lo_Register (
    .D(Lo_Content), .en(Update), .Q(Lo_Data), .clk(clock), .clr(Reset));

  // Other names for the same wires on the sheet: upd = Update
endmodule
