// Logisim project InstructionDecoder(Finished).circ as structural Verilog: 1 circuit, main circuit InstructionDecoder
module InstructionDecoder (
  input  [31:0] Instruction,
  input  ReadInstruction,
  output [4:0] DA_DataAddress,
  output [4:0] Rs,
  output [4:0] Rt,
  output [25:0] dest,
  output [15:0] OffSet,
  output [5:0] FuncCode,
  output [5:0] OpCode
);

  wire Clk;

  Clock clock_1 (.out(Clk));
  Register #(.width(32)) register_1 (
    .D(Instruction), .en(ReadInstruction), .Q({OpCode, dest[25:16], DA_DataAddress, dest[10:0]}), .clk(Clk));  // open: clr

  assign dest[15:11] = DA_DataAddress;
  assign FuncCode = dest[5:0];
  assign OffSet = {DA_DataAddress, dest[10:0]};
  assign Rs = dest[25:21];
  assign Rt = dest[20:16];

  // Other names for the same wires on the sheet: Instruction_t[31:0] = {OpCode, dest[25:16], DA_DataAddress, dest[10:0]};
  //   X[4:0] = dest[10:6]; RD[4:0] = DA_DataAddress; Write = ReadInstruction

  // Notes on the sheet:
  //   Instruction_Memory
  //   FuncCode
  //   RD
  //   Rt
  //   Rs
  //   OP-Code
  //   InstructionDecoder_Region
endmodule
