// Logisim project Memory_Controller(Finished).circ as structural Verilog: 2 circuits, main circuit Memory Controller
module Memory_Controller (
  input  [31:0] MemoryAddress,
  input  [31:0] Input_Word,
  input  [31:0] O0,
  input  [31:0] O1,
  input  [31:0] O2,
  input  [31:0] O3,
  input  R_W,
  input  Chip_Select,
  input  [3:0] Read_Time,
  input  [3:0] Write_Time,
  input  reset,
  input  clk,
  output [15:0] Address,
  output [31:0] OW_Out_Word,
  output [3:0] Mask,
  output [31:0] I0,
  output [31:0] I1,
  output [31:0] I2,
  output [31:0] I3,
  output Ram_Ready
);

  wire S0, S1, S2, S3;
  wire [3:0] multiplexer_2_out;
  wire [31:0] multiplexer_3_out, multiplexer_5_out, multiplexer_7_out;

  Decoder #(.select(2), .enable("false")) decoder_1 (
    .out0(Mask[0]), .out1(Mask[1]), .out2(Mask[2]), .out3(Mask[3]), .sel(MemoryAddress[3:2]));
  Multiplexer #(.width(32), .enable("false")) multiplexer_1 (
    .in0(O0), .in1({Input_Word[7:0], Input_Word[15:8], Input_Word[23:16], Input_Word[31:24]}), .out(I0),
    .sel(S0));
  Multiplexer #(.width(4), .disabled(0), .enable("false")) multiplexer_2 (
    .in0(Read_Time), .in1(Write_Time), .out(multiplexer_2_out), .sel(R_W));
  Multiplexer #(.width(32), .enable("false")) multiplexer_3 (
    .in0({32{1'b0}}), .in1(O0), .out(multiplexer_3_out), .sel(Mask[0]));
  Multiplexer #(.width(32), .enable("false")) multiplexer_4 (
    .in0(O1), .in1({Input_Word[7:0], Input_Word[15:8], Input_Word[23:16], Input_Word[31:24]}), .out(I1),
    .sel(S1));
  and and_1 (S0, R_W, Mask[0], Chip_Select);
  and and_2 (S2, R_W, Mask[2], Chip_Select);
  Multiplexer #(.width(32), .enable("false")) multiplexer_5 (
    .in0(multiplexer_3_out), .in1(O1), .out(multiplexer_5_out), .sel(Mask[1]));
  Multiplexer #(.width(32), .enable("false")) multiplexer_6 (
    .in0(O2), .in1({Input_Word[7:0], Input_Word[15:8], Input_Word[23:16], Input_Word[31:24]}), .out(I2),
    .sel(S2));
  Chronometer chronometer_1 (
    .WaitTime(multiplexer_2_out), .ChipSelect(Chip_Select), .Clock(clk), .Reset(reset), .Ready(Ram_Ready));
  Multiplexer #(.width(32), .enable("false")) multiplexer_7 (
    .in0(multiplexer_5_out), .in1(O2), .out(multiplexer_7_out), .sel(Mask[2]));
  and and_3 (S1, R_W, Mask[1], Chip_Select);
  and and_4 (S3, R_W, Mask[3], Chip_Select);
  Multiplexer #(.width(32), .enable("false")) multiplexer_8 (
    .in0(multiplexer_7_out), .in1(O3),
    .out({OW_Out_Word[7:0], OW_Out_Word[15:8], OW_Out_Word[23:16], OW_Out_Word[31:24]}), .sel(Mask[3]));
  Multiplexer #(.width(32), .enable("false")) multiplexer_9 (
    .in0(O3), .in1({Input_Word[7:0], Input_Word[15:8], Input_Word[23:16], Input_Word[31:24]}), .out(I3),
    .sel(S3));

  assign Address = MemoryAddress[19:4];

  // Other names for the same wires on the sheet: M0 = Mask[0]; M1 = Mask[1]; M2 = Mask[2]; M3 = Mask[3];
  //   decode_mask[1:0] = MemoryAddress[3:2]; RT[3:0] = Read_Time; Upd = Ram_Ready;
  //   Win[31:0] = {Input_Word[7:0], Input_Word[15:8], Input_Word[23:16], Input_Word[31:24]};
  //   Win_prime[31:0] = Input_Word; Wout[31:0] = OW_Out_Word;
  //   Wout_prime[31:0] = {OW_Out_Word[7:0], OW_Out_Word[15:8], OW_Out_Word[23:16], OW_Out_Word[31:24]};
  //   WT[3:0] = Write_Time

  // Notes on the sheet:
  //   Input/Output_Region
  //   Mask-Decoder
  //   Counter
  //   Read_BankSelector
  //   Write_BankSelector
endmodule

module Chronometer (
  input  [3:0] WaitTime,
  input  ChipSelect,
  input  Clock,
  input  Reset,
  output Ready
);

  wire [3:0] counter_1_q;

  Counter #(.width(4), .max('hf)) counter_1 (
    .count(ChipSelect), .Q(counter_1_q), .clk(Clock), .clr(Reset));  // open: load, D, carry
  Comparator #(.width(4), .mode("unsigned")) comparator_1 (.a(WaitTime), .b(counter_1_q), .eq(Ready));  // open: gt, lt
endmodule
