// Logisim project ProgramCounter(FInished).circ as structural Verilog: 1 circuit, main circuit ProgramCounter
module ProgramCounter (
  input  [31:0] jmp_addr,
  input  jmp_Jump,
  input  rst_Reset,
  input  fetch,
  input  clock,
  output [31:0] Q
);

  wire [31:0] adder_1_out, multiplexer_1_out;

  Register #(.width(32)) register_1 (.D(multiplexer_1_out), .en(fetch), .Q(Q), .clk(clock), .clr(rst_Reset));
  Adder #(.width(32)) adder_1 (.a(Q), .b(32'h4), .out(adder_1_out));  // open: cin, cout
  Multiplexer #(.width(32), .enable("false")) multiplexer_1 (
    .in0(adder_1_out), .in1(jmp_addr), .out(multiplexer_1_out), .sel(jmp_Jump));

  // Other names for the same wires on the sheet: clk = clock
endmodule
