// Logisim project Switcher_CU.circ as structural Verilog: 1 circuit, main circuit Switcher-CU
module Switcher_CU (
  input  [5:0] FuncCode,
  input  [5:0] OpCode,
  input  Main_In,
  output [12:0] SelectorCodes,
  output [3:0] ALU_OP,
  output [2:0] S_FC,
  output pop,
  output push,
  output Main_Out,
  output load,
  output store,
  output kbd_rnd,
  output TTY_Enable,
  output halt
);

  wire \and , and_1_out, and_3_out, and_6_out, and_7_out, and_8_out, and_9_out, and_10_out, and_15_out,
       and_20_out, and_21_out, and_22_out, and_23_out, and_24_out, and_25_out, and_26_out, and_27_out,
       and_28_out, and_29_out, and_30_out, and_31_out, and_32_out, and_33_out, and_34_out, and_35_out,
       and_36_out, and_37_out, and_38_out, and_39_out, and_40_out, and_41_out, and_42_out, and_43_out,
       and_45_out, comparator_1_eq, demultiplexer_5_out0, demultiplexer_5_out1, demultiplexer_6_out0,
       demultiplexer_8_out0, demultiplexer_8_out1, demultiplexer_9_out0, demultiplexer_9_out1, div, divu, ds,
       G_A, G_Aritm, G_Aritmetica, G_B, G_C, G_D, G_E, G_EI, G_J, G_Jr, G_L_S, G_PoP, Hi, kbd_rnd_t, Low, Lw,
       ms, mult, Mult_Div, multu, \nor , nor_1_out, nor_2_out, nor_3_out, nor_4_out, nor_5_out, nor_6_out,
       nor_7_out, nor_8_out, nor_9_out, nor_10_out, nor_11_out, nor_12_out, nor_13_out, nor_14_out,
       nor_15_out, nor_16_out, nor_17_out, nor_18_out, nor_19_out, nor_20_out, nor_21_out, nor_22_out,
       not_1_out, not_2_out, not_3_out, not_4_out, not_5_out, not_6_out, not_7_out, not_8_out, not_9_out,
       not_10_out, not_11_out, not_12_out, \or , or_4_out, or_5_out, or_7_out, Sw, tunnel, tunnel_t,
       tunnel_t_t, tunnel_t_t_t, tunnel_t_t_t_t, tunnel_t_t_t_t_t, tunnel_t_t_t_t_t_t, u, \xor ;
  wire [3:0] G_Selector;
  wire [12:0] undriven;

  Comparator #(.width(6)) comparator_1 (.a(OpCode), .b({6{1'b0}}), .eq(comparator_1_eq));  // open: gt, lt
  not not_1 (not_1_out, FuncCode[3]);
  not not_2 (not_2_out, FuncCode[5]);
  not not_3 (not_3_out, OpCode[1]);
  not not_4 (not_4_out, OpCode[3]);
  not not_5 (not_5_out, OpCode[4]);
  not not_6 (not_6_out, OpCode[5]);
  nor nor_1 (nor_1_out, G_C, G_J, G_D);
  not not_7 (not_7_out, OpCode[0]);
  Demultiplexer #(.enable("false")) demultiplexer_1 (.out0(Low), .out1(Hi), .in(G_E), .sel(FuncCode[1]));
  not not_8 (not_8_out, G_Jr);
  not not_9 (not_9_out, and_1_out);
  and and_1 (and_1_out, not_1_out, FuncCode[4], not_2_out);
  // OR_Gate or_1 has open pins: in0=FuncCode[0], in1=FuncCode[1], in2=FuncCode[2], in3=FuncCode[4], in4=FuncCode[5], out=open
  nor nor_2 (nor_2_out, FuncCode[0], FuncCode[1], FuncCode[2], FuncCode[4], FuncCode[5]);
  and and_2 (G_J, OpCode[1], nor_3_out);
  // OR_Gate or_2 has open pins: in0=OpCode[0], in1=OpCode[2], in2=OpCode[3], in3=OpCode[4], in4=OpCode[5], out=open
  nor nor_3 (nor_3_out, OpCode[0], OpCode[2], OpCode[3], OpCode[4], OpCode[5]);
  and and_3 (and_3_out, OpCode[0], nor_4_out);
  nor nor_4 (nor_4_out, OpCode[1], OpCode[2], OpCode[3], OpCode[4], OpCode[5]);
  // OR_Gate or_3 has open pins: in0=OpCode[1], in1=OpCode[2], in2=OpCode[3], in3=OpCode[4], in4=OpCode[5], out=open
  or or_4 (or_4_out, OpCode[0], OpCode[1], OpCode[2], OpCode[3]);
  nor nor_5 (nor_5_out, OpCode[4], OpCode[5]);
  and and_4 (G_PoP, not_7_out, OpCode[4], OpCode[5]);
  and and_5 (G_EI, OpCode[0], OpCode[4], OpCode[5]);
  Demultiplexer demultiplexer_2 (.out0(Lw), .out1(Sw), .in(1'b1), .sel(OpCode[3]), .en(and_7_out));
  and and_6 (and_6_out, OpCode[0], OpCode[1], OpCode[5]);
  and and_7 (and_7_out, and_6_out, nor_6_out);
  nor nor_6 (nor_6_out, OpCode[2], OpCode[4]);
  nor nor_7 (nor_7_out, div, divu, mult, multu);
  or or_5 (or_5_out, div, divu, mult, multu);
  not not_10 (not_10_out, FuncCode[0]);
  and and_8 (and_8_out, not_10_out, not_11_out);
  not not_11 (not_11_out, FuncCode[1]);
  and and_9 (and_9_out, FuncCode[1], not_12_out);
  not not_12 (not_12_out, FuncCode[0]);
  and and_10 (and_10_out, G_EI, ~kbd_rnd_t);  // AND_Gate
  Demultiplexer #(.enable("false")) demultiplexer_3 (
    .out0(TTY_Enable), .out1(halt), .in(and_10_out), .sel(FuncCode[1]));
  and and_11 (G_A, comparator_1_eq, not_8_out, not_9_out);
  and and_12 (G_E, comparator_1_eq, and_1_out);
  and and_13 (G_Jr, nor_2_out, comparator_1_eq, FuncCode[3]);
  and and_14 (G_C, not_3_out, OpCode[2], not_4_out, not_5_out, not_6_out);
  and and_15 (and_15_out, OpCode[1], OpCode[2], not_4_out, not_5_out, not_6_out);
  or or_6 (G_D, and_15_out, and_3_out);
  and and_16 (G_B, or_4_out, nor_5_out, nor_1_out);
  and and_17 (G_Aritmetica, nor_7_out, G_A);
  and and_18 (Mult_Div, or_5_out, G_A);
  or or_7 (or_7_out, and_8_out, and_9_out);
  or or_8 (G_L_S, Lw, Sw);
  and and_19 (kbd_rnd_t, G_EI, or_7_out);
  Multiplexer #(.select(4), .width(13), .enable("false")) multiplexer_1 (
    .in0(13'h4), .in1(13'h204), .in2(13'h8d), .in3(13'h402), .in4(13'h502), .in5(13'h2c), .in6(13'ha),
    .in7(13'h4c), .in8(13'h6c), .in9(13'hc08), .in10(13'h1408), .in11(undriven), .out(SelectorCodes),
    .sel(G_Selector));  // open: in12, in13, in14, in15
  Priority_Encoder #(.select(4)) priority_encoder_1 (
    .in0(G_Aritm), .in1(Mult_Div), .in2(G_B), .in3(G_C), .in4(G_D), .in5(kbd_rnd_t), .in6(TTY_Enable),
    .in7(Low), .in8(Hi), .in9(G_Jr), .in10(G_J), .in11(pop), .in12(push), .in13(store), .in14(load),
    .out(G_Selector));  // open: in15, gs, en_out, en_in
  Priority_Encoder priority_encoder_2 (
    .in0(1'b0), .in1(tunnel_t_t_t), .in2(u), .in3(tunnel_t_t_t_t), .in4(tunnel_t_t_t_t_t_t),
    .in5(tunnel_t_t_t_t_t), .in6(tunnel), .out(S_FC));  // open: in7, en_in, gs, en_out
  and and_20 (and_20_out, OpCode[1], OpCode[3]);
  and and_21 (and_21_out, FuncCode[0], FuncCode[2], FuncCode[4]);
  nor nor_8 (nor_8_out, OpCode[2], OpCode[4], OpCode[5]);
  and and_22 (and_22_out, OpCode[0], OpCode[1], OpCode[3]);
  and and_23 (and_23_out, FuncCode[0], FuncCode[1], FuncCode[3], FuncCode[5]);
  nor nor_9 (nor_9_out, FuncCode[2], FuncCode[4]);
  and and_24 (and_24_out, OpCode[1], OpCode[2]);
  and and_25 (and_25_out, and_24_out, nor_10_out);
  nor nor_10 (nor_10_out, OpCode[3], OpCode[4], OpCode[5]);
  nor nor_11 (nor_11_out, OpCode[1], OpCode[3], OpCode[4], OpCode[5]);
  nor nor_12 (nor_12_out, FuncCode[0], FuncCode[2], FuncCode[3], FuncCode[4]);
  and and_26 (and_26_out, OpCode[0], nor_13_out);
  nor nor_13 (nor_13_out, OpCode[1], OpCode[2], OpCode[3], OpCode[4], OpCode[5]);
  nor nor_14 (nor_14_out, OpCode[0], OpCode[2], OpCode[4], OpCode[5]);
  and and_27 (and_27_out, nor_14_out, and_20_out);
  nor nor_15 (nor_15_out, FuncCode[1], FuncCode[3], FuncCode[5]);
  and and_28 (and_28_out, nor_15_out, and_21_out);
  and and_29 (and_29_out, nor_8_out, and_22_out);
  and and_30 (and_30_out, and_23_out, nor_9_out);
  Demultiplexer demultiplexer_4 (
    .out0(tunnel_t_t_t_t), .out1(tunnel_t_t_t_t_t_t), .in(1'b1), .sel(OpCode[0]), .en(and_25_out));
  Demultiplexer demultiplexer_5 (
    .out0(demultiplexer_5_out0), .out1(demultiplexer_5_out1), .in(1'b1), .sel(OpCode[0]), .en(and_31_out));
  and and_31 (and_31_out, OpCode[2], nor_11_out);
  Demultiplexer demultiplexer_6 (
    .out0(demultiplexer_6_out0), .out1(tunnel_t_t), .in(1'b1), .sel(FuncCode[1]), .en(and_32_out));
  and and_32 (and_32_out, nor_12_out, FuncCode[5]);
  nor nor_16 (nor_16_out, OpCode[0], OpCode[1], OpCode[2], OpCode[4], OpCode[5]);
  and and_33 (and_33_out, nor_16_out, OpCode[3]);
  or or_9 (tunnel_t_t_t, and_26_out, and_27_out, and_28_out);
  or or_10 (u, and_29_out, and_30_out);
  or or_11 (tunnel_t_t_t_t_t, demultiplexer_5_out0, demultiplexer_5_out1);
  or or_12 (tunnel_t, demultiplexer_6_out0, and_33_out);
  Demultiplexer #(.enable("false")) demultiplexer_7 (.out0(ms), .out1(ds), .in(1'b1), .sel(FuncCode[1]));
  nor nor_17 (nor_17_out, FuncCode[2], FuncCode[5]);
  and and_34 (and_34_out, FuncCode[3], FuncCode[4]);
  Demultiplexer demultiplexer_8 (
    .out0(demultiplexer_8_out0), .out1(demultiplexer_8_out1), .in(1'b1), .sel(FuncCode[0]), .en(and_35_out));
  nor nor_18 (nor_18_out, FuncCode[1], FuncCode[3], FuncCode[4]);
  and and_35 (and_35_out, nor_18_out, and_36_out);
  and and_36 (and_36_out, FuncCode[2], FuncCode[5]);
  Demultiplexer demultiplexer_9 (
    .out0(demultiplexer_9_out0), .out1(demultiplexer_9_out1), .in(1'b1), .sel(OpCode[0]), .en(and_37_out));
  nor nor_19 (nor_19_out, OpCode[1], OpCode[4], OpCode[5]);
  and and_37 (and_37_out, nor_19_out, and_38_out);
  and and_38 (and_38_out, OpCode[2], OpCode[3]);
  and and_39 (and_39_out, FuncCode[0], FuncCode[1], FuncCode[2], FuncCode[5]);
  nor nor_20 (nor_20_out, FuncCode[3], FuncCode[4]);
  nor nor_21 (nor_21_out, FuncCode[0], FuncCode[1], FuncCode[2], FuncCode[4]);
  and and_40 (and_40_out, FuncCode[3], FuncCode[5]);
  and and_41 (and_41_out, OpCode[1], OpCode[2], OpCode[3]);
  and and_42 (and_42_out, and_41_out, nor_22_out);
  nor nor_22 (nor_22_out, OpCode[0], OpCode[4], OpCode[5]);
  // Priority_Encoder #(.select(4)) priority_encoder_3: pin names not known; wires that end beside it: 1'b0, tunnel_t_t_t_t_t_t, tunnel_t_t_t_t, tunnel_t_t_t_t_t, mult, multu, div, divu, ALU_OP, tunnel_t, tunnel_t_t, \and , \or , \nor , \xor , tunnel_t_t_t, u
  Demultiplexer demultiplexer_10 (.out0(div), .out1(divu), .in(ds), .sel(FuncCode[0]), .en(and_43_out));
  and and_43 (and_43_out, nor_17_out, and_34_out);
  Demultiplexer demultiplexer_11 (.out0(mult), .out1(multu), .in(ms), .sel(FuncCode[0]), .en(and_43_out));
  and and_44 (\nor , and_39_out, nor_20_out);
  and and_45 (and_45_out, nor_21_out, and_40_out);
  or or_13 (\xor , and_45_out, and_42_out);
  or or_14 (\and , demultiplexer_8_out0, demultiplexer_9_out0);
  or or_15 (\or , demultiplexer_8_out1, demultiplexer_9_out1);

  assign kbd_rnd = FuncCode[1];
  assign Main_Out = Main_In;

  // Other names for the same wires on the sheet: EI_Selector[1:0] = FuncCode[1:0]; Op[3:0] = ALU_OP;
  //   Selector_Codes[12:0] = SelectorCodes; tty = TTY_Enable

  // Notes on the sheet:
  //   Input_Otput_Region
  //   Decodificacion_por_grupo
  //   Pop_Push
  //   Especial_Ins
  //   Group_A
  //   Group_E
  //   Group_J
  //   Group_C
  //   Group_D
  //   Group_B
  //   Mapeo_Grupo_Selector
  //   Mapeo_Func_ALUCODE
endmodule
